# Fritzing sketch led_out (saved by Fritzing 0.9.3b)
circuit board: 8.46667cm x 5.64444cm
breadboards: 1

parts:
  R1 = Resistor [tolerance=±5% resistance=470 package="0805 [SMD]"]
  LED1 = LED - 5mm [color="Red (633nm)" package="5 mm [THT]"]
  Raspberry_Pi_1 = Raspberry Pi 3 [part_number=RPI-3-V1.2]

nets:
  N1: R1.Pin_0, Raspberry_Pi_1.GPIO18
  N2: R1.Pin_1, LED1.anode
  N3: LED1.cathode, Raspberry_Pi_1.GND

notes:
  GPIO18 (Pin 12)
