# Fritzing sketch button_external_pullUp (saved by Fritzing 0.9.3b)
circuit board: 8.46667cm x 5.64444cm
breadboards: 1

parts:
  S1 = Momentary Switch [package=ksa_sealed_tac_switch]
  R1 = Resistor [tolerance=±5% resistance=1.2k package="0805 [SMD]"]
  Raspberry_Pi_1 = Raspberry Pi 3 [part_number=RPI-3-V1.2]

nets:
  N1: S1.1, S1.2, R1.Pin_1, Raspberry_Pi_1.GPIO17
  N2: S1.3, S1.4, Raspberry_Pi_1.GND
  N3: R1.Pin_0, Raspberry_Pi_1.3v3

notes:
  GPIO17 (Pin 11)
