# Fritzing sketch button_internal_pullUp (saved by Fritzing 0.9.3b)
circuit board: 8.46667cm x 5.64444cm
breadboards: 1

parts:
  S1 = Momentary Switch [package=ksa_sealed_tac_switch]
  Raspberry_Pi_1 = Raspberry Pi 3 [part_number=RPI-3-V1.2]

nets:
  3V3: S1.1, S1.2, Raspberry_Pi_1.3v3, Raspberry_Pi_1.GPIO17, Raspberry_Pi_1.3V3
  N1: S1.3, S1.4, Raspberry_Pi_1.GND

notes:
  GPIO17 (Pin 11)
