# Fritzing sketch reaction_game2 (saved by Fritzing 0.9.9b)
breadboards: 1

parts:
  Raspberry_Pi_1 = Raspberry Pi 3 [part_number=RPI-3-V1.2]
  S1 = Pushbutton [package="[THT]"]
  LED1 = LED - 5mm [color="Red (633nm)" current=0.030 package="5 mm [THT]"]
  R1 = Resistor [tolerance=±5% power=0.25 resistance=330 package=THT]
  S2 = Pushbutton [package="[THT]"]

nets:
  N1: Raspberry_Pi_1.GPIO3, S2.Pin_3, S2.Pin_4
  N2: Raspberry_Pi_1.GPIO4, S1.Pin_1, S1.Pin_2
  N3: Raspberry_Pi_1.GND, S1.Pin_3, S1.Pin_4, R1.Pin_1, S2.Pin_1, S2.Pin_2
  N4: Raspberry_Pi_1.GPIO17, LED1.anode
  N5: LED1.cathode, R1.Pin_0

notes:
  Reaction Button
  Reset Button
