# Fritzing sketch buzzer (saved by Fritzing 0.9.9b)
breadboards: 1

parts:
  Raspberry_Pi_1 = Raspberry Pi 3 [part_number=RPI-3-V1.2]
  Part1 = KY-012 Active Buzzer Module [package="Breakout board"]

nets:
  N1: Raspberry_Pi_1.GPIO17, Part1.S
  N2: Raspberry_Pi_1.GND, Part1.-

custom parts:
  KY-012 Active Buzzer Module: Active Piezoelectric Buzzer Module Keyes KY-012, it produces single-tone sound when signal is high.
