# Fritzing sketch blink (saved by Fritzing 0.9.9b)
breadboards: 1

parts:
  Raspberry_Pi_1 = Raspberry Pi 3 [part_number=RPI-3-V1.2]
  R1 = Resistor [tolerance=±5% power=0.25 resistance=330 package=THT]
  LED1 = LED - 5mm [color="Red (633nm)" current=0.030 package="5 mm [THT]"]

nets:
  N1: Raspberry_Pi_1.GPIO17, LED1.anode
  N2: Raspberry_Pi_1.GND, R1.Pin_1
  N3: R1.Pin_0, LED1.cathode
