# Fritzing sketch traffic (saved by Fritzing 0.9.9b)
breadboards: 1

parts:
  Raspberry_Pi_1 = Raspberry Pi 3 [part_number=RPI-3-V1.2]
  R1 = Resistor [tolerance=±5% power=0.25 resistance=330 package=THT]
  LED1 = LED - 5mm [color="Red (633nm)" current=0.030 package="5 mm [THT]"]
  LED2 = LED - 5mm [color="Yellow (595nm)" current=0.030 package="5 mm [THT]"]
  R2 = Resistor [tolerance=±5% power=0.25 resistance=330 package=THT]

nets:
  N1: Raspberry_Pi_1.GND, R1.Pin_1, R2.Pin_1
  N2: Raspberry_Pi_1.GPIO17, LED1.anode
  N3: Raspberry_Pi_1.GPIO27, LED2.anode
  N4: R1.Pin_0, LED1.cathode
  N5: LED2.cathode, R2.Pin_0
