# Fritzing sketch alarm (saved by Fritzing 0.9.9b)
breadboards: 1

parts:
  Raspberry_Pi_1 = Raspberry Pi 3 [part_number=RPI-3-V1.2]
  Part1 = KY-012 Active Buzzer Module [package="Breakout board"]
  PIR1 = PIR sensor

nets:
  3V3: Raspberry_Pi_1.3v3, Raspberry_Pi_1.3V3, PIR1.VDD
  N1: Raspberry_Pi_1.GPIO4, PIR1.SIG
  N2: Raspberry_Pi_1.GPIO17, Part1.S
  GND: Raspberry_Pi_1.GND, Part1.-, PIR1.GND

custom parts:
  KY-012 Active Buzzer Module: Active Piezoelectric Buzzer Module Keyes KY-012, it produces single-tone sound when signal is high.
