# Fritzing sketch esp32_PIR2 (saved by Fritzing 0.9.9b)
breadboards: 1

parts:
  PIR1 = PIR sensor
  U1 = ESP32S-HiLetgo [part_number=ESP32S-HiLetgo]
  LED1 = LED - 5mm [color="Red (633nm)" current=0.030 package="5 mm [THT]"]
  R1 = Resistor [tolerance=±5% power=0.25 resistance=330 package=THT]
  Part1 = KY-004 Key Switch Module [package="Breakout board"]
  J1 = Piezo Speaker

nets:
  3.3V: PIR1.VDD, U1.3.3, Part1.Vin
  N1: PIR1.SIG, U1.GPIO19
  GND: PIR1.GND, U1.GND, LED1.cathode, Part1.-, J1.pin1
  N2: U1.GPIO15, Part1.S
  N3: U1.GPIO2, R1.Pin_0
  N4: U1.GPIO16, J1.pin2
  N5: LED1.anode, R1.Pin_1

custom parts:
  ESP32S-HiLetgo: HiLetgo ESP-WROOM-32 ESP32 ESP-32S Development Board 2.4GHz Dual-Mode WiFi + Bluetooth Dual Cores Microcontroller The ESP32 integrated with Antenna switches, RF Balun, power amplifiers, low-noise amplifiers, filters, and management modules, and the entire solution occupies the least area of PCB. 2.4 GHz Wi-Fi plus Bluetooth dual-mode chip, with TSMC Ultra-low power consumption 40nm technology,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
  KY-004 Key Switch Module: Arduino Key Switch Module Keyes KY-004 is a push button that will output a high signal when pressed.
