# Fritzing sketch ESP32-analog_read (saved by Fritzing 0.9.9b)

parts:
  U1 = ESP32S-HiLetgo [part_number=ESP32S-HiLetgo]
  Grove_Rotary_Angle_Sensor_(P)1 = Grove Rotary Angle Sensor (P)

nets:
  N1: U1.3.3, Grove_Rotary_Angle_Sensor_(P)1.VCC
  GND: U1.GND, Grove_Rotary_Angle_Sensor_(P)1.GND
  N2: U1.GPIO4, Grove_Rotary_Angle_Sensor_(P)1.SIG

custom parts:
  ESP32S-HiLetgo: HiLetgo ESP-WROOM-32 ESP32 ESP-32S Development Board 2.4GHz Dual-Mode WiFi + Bluetooth Dual Cores Microcontroller The ESP32 integrated with Antenna switches, RF Balun, power amplifiers, low-noise amplifiers, filters, and management modules, and the entire solution occupies the least area of PCB. 2.4 GHz Wi-Fi plus Bluetooth dual-mode chip, with TSMC Ultra-low power consumption 40nm technology,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
  Grove Rotary Angle Sensor (P): Rotary potentiometer, Grove connector, panel mount.
