# Fritzing sketch arduino_keypad (saved by Fritzing 0.9.9b)

parts:
  Keypad4x1 = Membran Keypad 4x4
  Componente1 = Arduino Uno (Rev3)

nets:
  N1: Keypad4x1.Pin1, Componente1.D11_PWM/MOSI
  N2: Keypad4x1.Pin2, Componente1.D10_PWM/SS
  N3: Keypad4x1.Pin3, Componente1.D9_PWM
  N4: Keypad4x1.Pin4, Componente1.D8
  N5: Keypad4x1.Pin5, Componente1.D7
  N6: Keypad4x1.Pin6, Componente1.D6_PWM
  N7: Keypad4x1.Pin7, Componente1.D5_PWM
  N8: Keypad4x1.Pin8, Componente1.D4

custom parts:
  Membran Keypad 4x4: Membrane Keypad 4x4 Matrix
