# Fritzing sketch esp32_keypad (saved by Fritzing 0.9.9b)

parts:
  Keypad4x1 = Membran Keypad 4x4
  U1 = ESP32S-HiLetgo [part_number=ESP32S-HiLetgo]

nets:
  N1: Keypad4x1.Pin1, U1.GPIO23
  N2: Keypad4x1.Pin2, U1.GPIO22
  N3: Keypad4x1.Pin3, U1.GPIO21
  N4: Keypad4x1.Pin4, U1.GPIO19
  N5: Keypad4x1.Pin5, U1.GPIO5
  N6: Keypad4x1.Pin6, U1.GPIO17
  N7: Keypad4x1.Pin7, U1.GPIO16
  N8: Keypad4x1.Pin8, U1.GPIO4

custom parts:
  Membran Keypad 4x4: Membrane Keypad 4x4 Matrix
  ESP32S-HiLetgo: HiLetgo ESP-WROOM-32 ESP32 ESP-32S Development Board 2.4GHz Dual-Mode WiFi + Bluetooth Dual Cores Microcontroller The ESP32 integrated with Antenna switches, RF Balun, power amplifiers, low-noise amplifiers, filters, and management modules, and the entire solution occupies the least area of PCB. 2.4 GHz Wi-Fi plus Bluetooth dual-mode chip, with TSMC Ultra-low power consumption 40nm technology,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
