# Fritzing sketch esp32_keypad2 (saved by Fritzing 0.9.9b)

parts:
  Keypad4x1 = Membran Keypad 4x4
  U1 = ESP32S-HiLetgo [part_number=ESP32S-HiLetgo]
  Part1 = KY-006 Passive Buzzer Module [package="Breakout board"]
  LED1 = LED - 5mm [color="Red (633nm)" current=0.030 package="5 mm [THT]"]
  R1 = Resistor [tolerance=±5% power=0.25 resistance=330 package=THT]

nets:
  N1: Keypad4x1.Pin1, U1.GPIO13
  N2: Keypad4x1.Pin2, U1.GPIO12
  N3: Keypad4x1.Pin3, U1.GPIO14
  N4: Keypad4x1.Pin4, U1.GPIO27
  N5: Keypad4x1.Pin5, U1.GPIO26
  N6: Keypad4x1.Pin6, U1.GPIO25
  N7: Keypad4x1.Pin7, U1.GPIO33
  N8: Keypad4x1.Pin8, U1.GPIO32
  GND: U1.GND, Part1.-, R1.Pin_1
  N9: U1.GPIO17, LED1.anode
  N10: U1.GPIO5, Part1.S
  N11: LED1.cathode, R1.Pin_0

custom parts:
  Membran Keypad 4x4: Membrane Keypad 4x4 Matrix
  ESP32S-HiLetgo: HiLetgo ESP-WROOM-32 ESP32 ESP-32S Development Board 2.4GHz Dual-Mode WiFi + Bluetooth Dual Cores Microcontroller The ESP32 integrated with Antenna switches, RF Balun, power amplifiers, low-noise amplifiers, filters, and management modules, and the entire solution occupies the least area of PCB. 2.4 GHz Wi-Fi plus Bluetooth dual-mode chip, with TSMC Ultra-low power consumption 40nm technology,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
  KY-006 Passive Buzzer Module: Passive Piezoelectric Buzzer Module Keyes KY-006, it can produce a range of sound tones depending on the input frequency.
