# Fritzing sketch lcd-counter (saved by Fritzing 0.9.9b)
breadboards: 1

parts:
  LCD1 = LCD screen
  R1 = Trimmer Potentiometer [maximum_resistance=10kΩ package=THT]
  U1 = ESP32S-HiLetgo [part_number=ESP32S-HiLetgo]

nets:
  GND: LCD1.VSS, LCD1.R/W, LCD1.LED-, R1.leg1, U1.GND
  VDD: LCD1.VDD, LCD1.LED+, R1.leg2, U1.VIN
  N1: LCD1.V0, R1.wiper
  N2: LCD1.RS, U1.GPIO22
  N3: LCD1.E, U1.GPIO23
  N4: LCD1.DB4, U1.GPIO4
  N5: LCD1.DB5, U1.GPIO0
  N6: LCD1.DB6, U1.GPIO2
  N7: LCD1.DB7, U1.GPIO15

custom parts:
  ESP32S-HiLetgo: HiLetgo ESP-WROOM-32 ESP32 ESP-32S Development Board 2.4GHz Dual-Mode WiFi + Bluetooth Dual Cores Microcontroller The ESP32 integrated with Antenna switches, RF Balun, power amplifiers, low-noise amplifiers, filters, and management modules, and the entire solution occupies the least area of PCB. 2.4 GHz Wi-Fi plus Bluetooth dual-mode chip, with TSMC Ultra-low power consumption 40nm technology,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
