# Fritzing sketch esp32_keypad_lcd (saved by Fritzing 0.9.9b)
breadboards: 1

parts:
  Keypad4x1 = Membran Keypad 4x4
  U1 = ESP32S-HiLetgo [part_number=ESP32S-HiLetgo]
  Part1 = KY-006 Passive Buzzer Module [package="Breakout board"]
  R1 = Resistor [tolerance=±5% power=0.25 resistance=330 package=THT]
  LCD1 = LCD screen
  LED2 = LED - 5mm [color="Red (633nm)" current=0.030 package="5 mm [THT]"]
  R2 = Rotary Potentiometer (Small) [maximum_resistance=100kΩ package=THT]

nets:
  N1: Keypad4x1.Pin1, U1.GPIO13
  N2: Keypad4x1.Pin2, U1.GPIO12
  N3: Keypad4x1.Pin3, U1.GPIO14
  N4: Keypad4x1.Pin4, U1.GPIO27
  N5: Keypad4x1.Pin5, U1.GPIO26
  N6: Keypad4x1.Pin6, U1.GPIO25
  N7: Keypad4x1.Pin7, U1.GPIO33
  N8: Keypad4x1.Pin8, U1.GPIO32
  GND: U1.GND, Part1.-, R1.Pin_1, LCD1.VSS, LCD1.R/W, LCD1.LED-, R2.leg2
  VIN: U1.VIN, LCD1.VDD, LCD1.LED+, R2.leg1
  DB7: U1.GPIO15, LCD1.DB7
  DB6: U1.GPIO2, LCD1.DB6
  DB5: U1.GPIO0, LCD1.DB5
  DB4: U1.GPIO4, LCD1.DB4
  N9: U1.GPIO17, LED2.anode
  N10: U1.GPIO5, Part1.S
  N11: U1.GPIO22, LCD1.RS
  N12: U1.GPIO23, LCD1.E
  N13: R1.Pin_0, LED2.cathode
  N14: LCD1.V0, R2.wiper

custom parts:
  Membran Keypad 4x4: Membrane Keypad 4x4 Matrix
  ESP32S-HiLetgo: HiLetgo ESP-WROOM-32 ESP32 ESP-32S Development Board 2.4GHz Dual-Mode WiFi + Bluetooth Dual Cores Microcontroller The ESP32 integrated with Antenna switches, RF Balun, power amplifiers, low-noise amplifiers, filters, and management modules, and the entire solution occupies the least area of PCB. 2.4 GHz Wi-Fi plus Bluetooth dual-mode chip, with TSMC Ultra-low power consumption 40nm technology,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
  KY-006 Passive Buzzer Module: Passive Piezoelectric Buzzer Module Keyes KY-006, it can produce a range of sound tones depending on the input frequency.
