# Fritzing sketch ESP32-serial2 (saved by Fritzing 0.9.9b)
breadboards: 1

parts:
  U1 = ESP32S-HiLetgo [part_number=ESP32S-HiLetgo]
  Part1 = KY-016 RGB Full Color LED Module [package="Breakout board"]
  Part2 = KY-004 Key Switch Module [package="Breakout board"]

nets:
  N1: U1.3.3, Part2.Vin
  N2: U1.GND, Part1.-, Part2.-
  N3: U1.GPIO17, Part2.S
  N4: U1.GPIO5, Part1.R
  N5: U1.GPIO18, Part1.G
  N6: U1.GPIO19, Part1.B

custom parts:
  ESP32S-HiLetgo: HiLetgo ESP-WROOM-32 ESP32 ESP-32S Development Board 2.4GHz Dual-Mode WiFi + Bluetooth Dual Cores Microcontroller The ESP32 integrated with Antenna switches, RF Balun, power amplifiers, low-noise amplifiers, filters, and management modules, and the entire solution occupies the least area of PCB. 2.4 GHz Wi-Fi plus Bluetooth dual-mode chip, with TSMC Ultra-low power consumption 40nm technology,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
  KY-016 RGB Full Color LED Module: KY-016 Arduino full color 5mm RGB LED, different colors can be obtained by mixing the three primary colors.
  KY-004 Key Switch Module: Arduino Key Switch Module Keyes KY-004 is a push button that will output a high signal when pressed.
