# Fritzing sketch ESP32-serial3 (saved by Fritzing 0.9.9b)

parts:
  U1 = ESP32S-HiLetgo [part_number=ESP32S-HiLetgo]
  Part1 = KY-023 Dual Axis Joystick Module [package="Breakout board"]
  Part2 = KY-009 Full Color RGB LED SMD Module [package="Breakout board"]

nets:
  N1: U1.3.3, Part1.+5V
  GND: U1.GND, Part1.GND, Part2.-
  N2: U1.GPIO15, Part1.SW
  N3: U1.GPIO2, Part1.VRx
  N4: U1.GPIO4, Part1.VRy
  N5: U1.GPIO5, Part2.B
  N6: U1.GPIO18, Part2.G
  N7: U1.GPIO19, Part2.R

custom parts:
  ESP32S-HiLetgo: HiLetgo ESP-WROOM-32 ESP32 ESP-32S Development Board 2.4GHz Dual-Mode WiFi + Bluetooth Dual Cores Microcontroller The ESP32 integrated with Antenna switches, RF Balun, power amplifiers, low-noise amplifiers, filters, and management modules, and the entire solution occupies the least area of PCB. 2.4 GHz Wi-Fi plus Bluetooth dual-mode chip, with TSMC Ultra-low power consumption 40nm technology,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
  KY-023 Dual Axis Joystick Module: X/Y Analog Joystick KEYES KY-023 module. It contains two potentiometers and a button.
  KY-009 Full Color RGB LED SMD Module: RGB full color LED Module KY-009 for Arduino, emits a range of colors by mixing red, green and blue. The amount of each primary color is adjusted using PWM.
