# Fritzing sketch dh11-arduino (saved by Fritzing 0.9.9b)

parts:
  Componente1 = Arduino Uno (Rev3)
  Part1 = KY-015 Temperature & Humidity Sensor Module [package="Breakout board"]

nets:
  N1: Componente1.D2, Part1.S
  5V: Componente1.5V, Part1.Vin
  N2: Componente1.GND, Part1.-

custom parts:
  KY-015 Temperature & Humidity Sensor Module: DH-11 temperature and humidity sensor in KEYES KY-015 module, provides a low-latency serial interface to measure humidity and temperature.
