# Fritzing sketch dh11_lcd-arduino (saved by Fritzing 0.9.9b)
breadboards: 1

parts:
  Componente1 = Arduino Uno (Rev3)
  Part1 = KY-015 Temperature & Humidity Sensor Module [package="Breakout board"]
  LCD1 = LCD screen
  R1 = Trimmer Potentiometer [maximum_resistance=10kΩ package=THT]

nets:
  N1: Componente1.D8, Part1.S
  N2: Componente1.D11_PWM/MOSI, LCD1.E
  N3: Componente1.D12/MISO, LCD1.RS
  N4: Componente1.D2, LCD1.DB7
  N5: Componente1.D3_PWM, LCD1.DB6
  N6: Componente1.D4, LCD1.DB5
  N7: Componente1.D5_PWM, LCD1.DB4
  5V: Componente1.5V, Part1.Vin, LCD1.VDD, LCD1.LED+, R1.leg2
  GND: Componente1.GND, Part1.-, LCD1.VSS, LCD1.R/W, LCD1.LED-, R1.leg1
  N8: LCD1.V0, R1.wiper

custom parts:
  KY-015 Temperature & Humidity Sensor Module: DH-11 temperature and humidity sensor in KEYES KY-015 module, provides a low-latency serial interface to measure humidity and temperature.
