# Fritzing sketch dh11_lcd-esp32 (saved by Fritzing 0.9.9b)
breadboards: 1

parts:
  Part1 = KY-015 Temperature & Humidity Sensor Module [package="Breakout board"]
  LCD1 = LCD screen
  R1 = Trimmer Potentiometer [maximum_resistance=10kΩ package=THT]
  U1 = ESP32S-HiLetgo [part_number=ESP32S-HiLetgo]

nets:
  N1: Part1.S, U1.GPIO19
  VIN: Part1.Vin, LCD1.VDD, LCD1.LED+, R1.leg2, U1.VIN
  VSS: Part1.-, LCD1.VSS, LCD1.R/W, LCD1.LED-, R1.leg1, U1.GND
  N2: LCD1.V0, R1.wiper
  N3: LCD1.RS, U1.GPIO22
  N4: LCD1.E, U1.GPIO23
  N5: LCD1.DB4, U1.GPIO4
  N6: LCD1.DB5, U1.GPIO0
  N7: LCD1.DB6, U1.GPIO2
  N8: LCD1.DB7, U1.GPIO15

custom parts:
  KY-015 Temperature & Humidity Sensor Module: DH-11 temperature and humidity sensor in KEYES KY-015 module, provides a low-latency serial interface to measure humidity and temperature.
  ESP32S-HiLetgo: HiLetgo ESP-WROOM-32 ESP32 ESP-32S Development Board 2.4GHz Dual-Mode WiFi + Bluetooth Dual Cores Microcontroller The ESP32 integrated with Antenna switches, RF Balun, power amplifiers, low-noise amplifiers, filters, and management modules, and the entire solution occupies the least area of PCB. 2.4 GHz Wi-Fi plus Bluetooth dual-mode chip, with TSMC Ultra-low power consumption 40nm technology,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
