# Fritzing sketch ESP_ic2_lcd (saved by Fritzing 0.9.9b)

parts:
  Componente1 = LCD1602-I2C
  U1 = ESP32S-HiLetgo [part_number=ESP32S-HiLetgo]
  Part1 = KY-015 Temperature & Humidity Sensor Module [package="Breakout board"]

nets:
  GND: Componente1.GND, U1.GND, Part1.-
  VCC: Componente1.VCC, U1.VIN
  N1: Componente1.SDA, U1.GPIO21
  N2: Componente1.SCL, U1.GPIO22
  N3: U1.3.3, Part1.Vin
  N4: U1.GPIO2, Part1.S

custom parts:
  LCD1602-I2C: A standard character display, usually with 2x16 characters. Comes in many colors with LCM1602 IIC attached.
  ESP32S-HiLetgo: HiLetgo ESP-WROOM-32 ESP32 ESP-32S Development Board 2.4GHz Dual-Mode WiFi + Bluetooth Dual Cores Microcontroller The ESP32 integrated with Antenna switches, RF Balun, power amplifiers, low-noise amplifiers, filters, and management modules, and the entire solution occupies the least area of PCB. 2.4 GHz Wi-Fi plus Bluetooth dual-mode chip, with TSMC Ultra-low power consumption 40nm technology,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
  KY-015 Temperature & Humidity Sensor Module: DH-11 temperature and humidity sensor in KEYES KY-015 module, provides a low-latency serial interface to measure humidity and temperature.
