# Fritzing sketch ESP32-temperatura (saved by Fritzing 0.9.9b)

parts:
  Part1 = KY-013 Analog Temperature Sensor Module [package="Breakout board"]
  U1 = ESP32S-HiLetgo [part_number=ESP32S-HiLetgo]

nets:
  N1: Part1.S, U1.GPIO21
  N2: Part1.Vin, U1.3.3
  N3: Part1.-, U1.GND

custom parts:
  KY-013 Analog Temperature Sensor Module: KY-013 Analog Temperature Sensor module, measures ambient temperature based on resistance of the thermistor.
  ESP32S-HiLetgo: HiLetgo ESP-WROOM-32 ESP32 ESP-32S Development Board 2.4GHz Dual-Mode WiFi + Bluetooth Dual Cores Microcontroller The ESP32 integrated with Antenna switches, RF Balun, power amplifiers, low-noise amplifiers, filters, and management modules, and the entire solution occupies the least area of PCB. 2.4 GHz Wi-Fi plus Bluetooth dual-mode chip, with TSMC Ultra-low power consumption 40nm technology,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
