# Fritzing sketch PIR_MQTT_esp32 (saved by Fritzing 0.9.9b)

parts:
  HC-SR1 = HC-SR501 Body Sensor Module
  U1 = ESP32S-HiLetgo [part_number=ESP32S-HiLetgo]

nets:
  N1: HC-SR1.VCC, U1.3.3
  N2: HC-SR1.OUT, U1.GPIO5
  N3: HC-SR1.GND, U1.GPIO19

custom parts:
  HC-SR501 Body Sensor Module: Pyroelectric Infrared PIR Motion Sensor Detector Module
  ESP32S-HiLetgo: HiLetgo ESP-WROOM-32 ESP32 ESP-32S Development Board 2.4GHz Dual-Mode WiFi + Bluetooth Dual Cores Microcontroller The ESP32 integrated with Antenna switches, RF Balun, power amplifiers, low-noise amplifiers, filters, and management modules, and the entire solution occupies the least area of PCB. 2.4 GHz Wi-Fi plus Bluetooth dual-mode chip, with TSMC Ultra-low power consumption 40nm technology,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
